// Digital circuit bench.dig as structural Verilog
module bench (
  input  clk,
  input  [15:0] in_2
);

  wire and_1_out, dipswitch_1_out, dipswitch_2_out, dipswitch_3_out, reset_1_out, u_fullAdder_c_out;
  wire [15:0] u_ctr_out, u_fullAdder_sum;

  Reset reset_1 (.out(reset_1_out));
  and and_1 (and_1_out, clk, reset_1_out);
  DipSwitch dipswitch_1 (.out(dipswitch_1_out));
  DipSwitch dipswitch_2 (.out(dipswitch_2_out));
  ctr #(.applicationType("IVERILOG"), .CodeFile("/home/neon/src/bench/ctr.v")) u_ctr (
    .up_down(dipswitch_1_out), .clk(and_1_out), .rstn(dipswitch_2_out), .out(u_ctr_out));
  DipSwitch dipswitch_3 (.out(dipswitch_3_out));
  fullAdder #(.applicationType("IVERILOG"), .CodeFile("/home/neon/src/bench/adder.v")) u_fullAdder (
    .a(u_ctr_out), .b(in_2), .c_in(dipswitch_3_out), .c_out(u_fullAdder_c_out), .sum(u_fullAdder_sum));
  LED led_1 (.in(u_fullAdder_c_out));
  // Probe on u_fullAdder_sum

  // Notes on the sheet:
  //   clk: Hz: 10
endmodule
